// Logisim project Project sum and carry.circ as structural Verilog: 1 circuit, main circuit main
module main (
  input  A,
  input  B,
  input  C,
  input  D,
  input  E,
  output Carry,
  output W,
  output X,
  output Y,
  output Z
);

  wire and_1_out, and_2_out, and_3_out, and_4_out, and_5_out, and_6_out, and_7_out, and_8_out, and_9_out,
       and_10_out, and_11_out, and_12_out, and_13_out, not_1_out, not_2_out, not_3_out, not_4_out, or_1_out,
       or_2_out, or_6_out;

  not not_1 (not_1_out, B);
  not not_2 (not_2_out, A);
  not not_3 (not_3_out, C);
  not not_4 (not_4_out, D);
  and and_1 (and_1_out, B, C);
  and and_2 (and_2_out, B, D);
  and and_3 (and_3_out, A, D);
  and and_4 (and_4_out, B, not_3_out);
  and and_5 (and_5_out, C, D);
  and and_6 (and_6_out, C, not_1_out);
  and and_7 (and_7_out, A, not_4_out);
  and and_8 (and_8_out, not_2_out, not_1_out);
  and and_9 (and_9_out, not_4_out, C);
  and and_10 (and_10_out, not_4_out, A);
  or or_1 (or_1_out, A, and_1_out);
  and and_11 (and_11_out, and_4_out, not_4_out);
  or or_2 (or_2_out, and_6_out, and_7_out);
  and and_12 (and_12_out, and_8_out, D);
  and and_13 (and_13_out, and_9_out, B);
  or or_3 (Carry, or_1_out, and_2_out);
  or or_4 (W, and_3_out, and_11_out);
  or or_5 (X, and_5_out, or_2_out);
  or or_6 (or_6_out, and_12_out, and_13_out);
  or or_7 (Y, or_6_out, and_10_out);

  assign Z = E;
endmodule
